# Fritzing sketch schematics (saved by Fritzing 1.0.4)
breadboards: 2

parts:
  S1 = Pushbutton [package="[THT]"]
  S2 = Pushbutton [package="[THT]"]
  LED1 = smd LED [color="Red (633nm)" package="1206 [SMD]"]
  LED2 = smd LED [color="Green (555nm)" package="1206 [SMD]"]
  LED3 = smd LED [color="Blue (525nm)" package="1206 [SMD]"]
  LED4 = smd LED [color="Blue (525nm)" package="1206 [SMD]"]
  LED5 = smd LED [color="Blue (525nm)" package="1206 [SMD]"]
  R1 = Resistor [tolerance=±5% resistance=100 package="0402 [SMD]"]
  SG1 = Buzzer 12mm [part_number=COM-07950 package=buzzer-12mm-ns]
  S3 = Pushbutton [package="[THT]"]
  R2 = Resistor [tolerance=±5% resistance=220 package="2010 [SMD]"]
  Disp1 = 60mm 8x8 dot matrix column cathode led display with standard pcb pads
  LCD1 = LCD screen
  LCD3 = LCD screen
  LCD2 = LCD screen
  U1 = LIPO-1000mAh [package=lipo-1000]
  Composant1 = Arduino Mega 2560 (Rev3)

nets:
  VSS: S1.Pin_1, S1.Pin_2, S2.Pin_1, S2.Pin_2, SG1.2, S3.Pin_1, S3.Pin_2, Disp1.pin_12, LCD1.VSS, LCD1.V0, LCD1.R/W, LCD1.LED-, LCD3.VSS, LCD3.V0, LCD3.R/W, LCD3.LED-, LCD2.VSS, LCD2.V0, LCD2.R/W, LCD2.LED-, U1.-, Composant1.GND
  N1: S1.Pin_3, S1.Pin_4, Composant1.D13_PWM
  N2: S2.Pin_3, S2.Pin_4, Composant1.D12_PWM
  N3: LED1.cathode, Composant1.D10_PWM
  VDD: LED1.anode, LED2.anode, LED3.anode, LED4.anode, LED5.anode, R1.Pin_0, R1.Pin_1, R2.Pin_1, Disp1.pin_16, LCD1.VDD, LCD1.LED+, LCD3.VDD, LCD3.LED+, LCD2.VDD, LCD2.LED+, U1.+, Composant1.VIN
  N4: LED2.cathode, Composant1.D9_PWM
  N5: LED3.cathode, Composant1.D6_PWM
  N6: LED4.cathode, Composant1.D8_PWM
  N7: LED5.cathode, Composant1.D7_PWM
  N8: SG1.1, Composant1.D5_PWM
  N9: S3.Pin_3, S3.Pin_4, Composant1.D11_PWM
  N10: Disp1.pin_13, Composant1.D51
  N11: Disp1.pin_14, Composant1.D53
  N12: Disp1.pin_15, Composant1.D52
  N13: LCD1.RS, Composant1.D22
  N14: LCD1.E, Composant1.D23
  N15: LCD1.DB4, Composant1.D24
  N16: LCD1.DB5, Composant1.D25
  N17: LCD1.DB6, Composant1.D26
  N18: LCD1.DB7, Composant1.D27
  N19: LCD3.RS, Composant1.D34
  N20: LCD3.E, Composant1.D35
  N21: LCD3.DB4, Composant1.D36
  N22: LCD3.DB5, Composant1.D37
  N23: LCD3.DB6, Composant1.D38
  N24: LCD3.DB7, Composant1.D39
  N25: LCD2.RS, Composant1.D28
  N26: LCD2.E, Composant1.D29
  N27: LCD2.DB4, Composant1.D30
  N28: LCD2.DB5, Composant1.D31
  N29: LCD2.DB6, Composant1.D32
  N30: LCD2.DB7, Composant1.D33

notes:
  VCC : Rouge
  CLK: Vert
  CE: Violet
  MOSI: Cyan
  GND: Noir
  Alimentation de 5v, 2a

custom parts:
  Buzzer 12mm: Buzzer 12mm Spark Fun Electronics SKU : Comp-Buzzer Through hole This is a small 12mm round speaker that operates around the audible 2kHz range. You can use these speakers to create simple music or user interfaces. This is not a true piezoelectric speaker but behaves similarly. Instead of a piezoelectric crystal that vibrates with an electric current, this tiny speaker uses an electromagnet to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
